// Logisim project ex4.circ as structural Verilog: 1 circuit, main circuit Split
module Split (
  input  [7:0] In1,
  output Out1,
  output [7:0] Out2
);

  and and_1 (Out1, In1[0], In1[7]);
  not not_1 (Out2[7], In1[7]);

  assign Out2[6:0] = In1[6:0];

  // Other names for the same wires on the sheet: in_7 = In1[7]; in_0 = In1[0]; mid_6[5:0] = In1[6:1]

  // Notes on the sheet:
  //   PUT CIRCUITRY HERE
endmodule
