// Logisim project ex5.circ as structural Verilog: 5 circuits, main circuit rotr
module rotr (
  input  [15:0] A,
  input  [3:0] B,
  output [15:0] Out1
);

  wire [3:0] B_2, not_1_out;
  wire [15:0] A_1, A_2, multiplexer_1_out, multiplexer_2_out, multiplexer_3_out, multiplexer_4_out,
       multiplexer_5_out, multiplexer_6_out, rot1_1_out_3, rot1_2_out_3, rot2_1_out_3, rot2_2_out_3,
       rot4_1_out_3, rot4_2_out_3, rot8_1_out_3, rot8_2_out_3;

  assign not_1_out = ~B;  // NOT_Gate not_1, 4 bits wide
  rot8 rot8_1 (.in_1(A), .in_2(1'b1), .out_3(rot8_1_out_3));
  Multiplexer #(.enable("false"), .width(16)) multiplexer_1 (
    .in0(A), .in1(rot8_2_out_3), .out(multiplexer_1_out), .sel(B[3]));
  rot8 rot8_2 (.in_1(A), .in_2(1'b0), .out_3(rot8_2_out_3));
  Adder #(.width(4)) adder_1 (.a(4'b0001), .b(not_1_out), .out(B_2));  // open: cin, cout
  Multiplexer #(.enable("false"), .width(16)) multiplexer_2 (
    .in0(A), .in1(rot8_1_out_3), .out(multiplexer_2_out), .sel(B_2[3]));
  rot4 rot4_1 (.in_1(multiplexer_1_out), .in_2(1'b0), .out_3(rot4_1_out_3));
  rot4 rot4_2 (.in_1(multiplexer_2_out), .in_2(1'b1), .out_3(rot4_2_out_3));
  Multiplexer #(.enable("false"), .width(16)) multiplexer_3 (
    .in0(multiplexer_1_out), .in1(rot4_1_out_3), .out(multiplexer_3_out), .sel(B[2]));
  Multiplexer #(.enable("false"), .width(16)) multiplexer_4 (
    .in0(multiplexer_2_out), .in1(rot4_2_out_3), .out(multiplexer_4_out), .sel(B_2[2]));
  rot2 rot2_1 (.in_1(multiplexer_3_out), .in_2(1'b0), .out_3(rot2_1_out_3));
  rot2 rot2_2 (.in_1(multiplexer_4_out), .in_2(1'b1), .out_3(rot2_2_out_3));
  Multiplexer #(.enable("false"), .width(16)) multiplexer_5 (
    .in0(multiplexer_4_out), .in1(rot2_2_out_3), .out(multiplexer_5_out), .sel(B_2[1]));
  Multiplexer #(.enable("false"), .width(16)) multiplexer_6 (
    .in0(multiplexer_3_out), .in1(rot2_1_out_3), .out(multiplexer_6_out), .sel(B[1]));
  rot1 rot1_1 (.in_1(multiplexer_5_out), .in_2(1'b1), .out_3(rot1_1_out_3));
  rot1 rot1_2 (.in_1(multiplexer_6_out), .in_2(1'b0), .out_3(rot1_2_out_3));
  Multiplexer #(.enable("false"), .width(16)) multiplexer_7 (
    .in0(multiplexer_6_out), .in1(rot1_2_out_3), .out(A_1), .sel(B[0]));
  Multiplexer #(.enable("false"), .width(16)) multiplexer_8 (
    .in0(multiplexer_5_out), .in1(rot1_1_out_3), .out(A_2), .sel(B_2[0]));
  assign Out1 = A_1 | A_2;  // OR_Gate or_1, 16 bits wide

  // Notes on the sheet:
  //   PUT CIRCUITRY HERE
endmodule

module rot8 (
  input  [15:0] in_1,
  input  in_2,
  output [15:0] out_3
);

  wire [15:0] bit_extender_1_out;

  assign bit_extender_1_out = {{8{1'b0}}, in_1[15:8]};  // Bit_Extender bit_extender_1
  Multiplexer #(.enable("false"), .width(16)) multiplexer_1 (
    .in0(bit_extender_1_out), .in1({in_1[7:0], {8{1'b0}}}), .out(out_3), .sel(in_2));

  // Notes on the sheet:
  //   PUT CIRCUITRY HERE
endmodule

module rot4 (
  input  [15:0] in_1,
  input  in_2,
  output [15:0] out_3
);

  wire [15:0] bit_extender_1_out;

  assign bit_extender_1_out = {{4{1'b0}}, in_1[15:4]};  // Bit_Extender bit_extender_1
  Multiplexer #(.enable("false"), .width(16)) multiplexer_1 (
    .in0(bit_extender_1_out), .in1({in_1[11:0], 4'b0000}), .out(out_3), .sel(in_2));

  // Notes on the sheet:
  //   PUT CIRCUITRY HERE
endmodule

module rot2 (
  input  [15:0] in_1,
  input  in_2,
  output [15:0] out_3
);

  wire [15:0] bit_extender_1_out;

  assign bit_extender_1_out = {{2{1'b0}}, in_1[15:2]};  // Bit_Extender bit_extender_1
  Multiplexer #(.enable("false"), .width(16)) multiplexer_1 (
    .in0(bit_extender_1_out), .in1({in_1[13:0], 2'b00}), .out(out_3), .sel(in_2));

  // Notes on the sheet:
  //   PUT CIRCUITRY HERE
endmodule

module rot1 (
  input  [15:0] in_1,
  input  in_2,
  output [15:0] out_3
);

  wire [15:0] bit_extender_1_out;

  assign bit_extender_1_out = {{1{1'b0}}, in_1[15:1]};  // Bit_Extender bit_extender_1
  Multiplexer #(.enable("false"), .width(16)) multiplexer_1 (
    .in0(bit_extender_1_out), .in1({in_1[14:0], 1'b0}), .out(out_3), .sel(in_2));

  // Notes on the sheet:
  //   PUT CIRCUITRY HERE
endmodule
